// Logisim project TallerLogica-Combinatorios.circ as structural Verilog: 15 circuits, main circuit verificador
module sumador_simple (
  input  a,
  input  b,
  output S,
  output Cout
);

  xor xor_1 (S, a, b);
  and and_1 (Cout, a, b);
endmodule

module sumador_completo (
  input  Cin,
  input  A,
  input  B,
  output S,
  output Cout
);

  wire sumador_simple_1_cout, sumador_simple_1_s, sumador_simple_2_cout;

  sumador_simple sumador_simple_1 (.a(A), .b(B), .S(sumador_simple_1_s), .Cout(sumador_simple_1_cout));
  sumador_simple sumador_simple_2 (.a(Cin), .b(sumador_simple_1_s), .S(S), .Cout(sumador_simple_2_cout));
  or or_1 (Cout, sumador_simple_2_cout, sumador_simple_1_cout);
endmodule

module sumador_4 (
  input  Cin,
  input  [3:0] A,
  input  [3:0] B,
  output [3:0] S,
  output Cout
);

  wire sumador_completo_1_cout, sumador_completo_2_cout, sumador_completo_3_cout;

  sumador_completo sumador_completo_1 (.A(A[0]), .B(B[0]), .Cin(Cin), .S(S[0]), .Cout(sumador_completo_1_cout));
  sumador_completo sumador_completo_2 (
    .A(A[1]), .B(B[1]), .Cin(sumador_completo_1_cout), .S(S[1]), .Cout(sumador_completo_2_cout));
  sumador_completo sumador_completo_3 (
    .A(A[2]), .B(B[2]), .Cin(sumador_completo_2_cout), .S(S[2]), .Cout(sumador_completo_3_cout));
  sumador_completo sumador_completo_4 (.A(A[3]), .B(B[3]), .Cin(sumador_completo_3_cout), .S(S[3]), .Cout(Cout));
  Hex_Digit_Display hex_digit_display_1 (.value(S));  // open: dp
endmodule

module comparador_cero (
  input  [3:0] A,
  output Z
);

  wire not_1_out, not_2_out, not_3_out, not_4_out;

  not not_1 (not_1_out, A[0]);
  not not_2 (not_2_out, A[1]);
  not not_3 (not_3_out, A[2]);
  not not_4 (not_4_out, A[3]);
  and and_1 (Z, not_1_out, not_2_out, not_3_out, not_4_out);
endmodule

module sumador_flags (
  input  Cin,
  input  [3:0] A,
  input  [3:0] B,
  output [3:0] S,
  output N,
  output Z,
  output V,
  output C
);

  sumador_4 sumador_4_1 (.Cin(Cin), .A(A), .S({N, S[2:0]}), .B(B), .Cout(C));
  Hex_Digit_Display hex_digit_display_1 (.value({N, S[2:0]}));  // open: dp
  overflow overflow_1 (.A_n(A[3]), .B_n(B[3]), .S_n(N), .OV(V));
  comparador_cero comparador_cero_1 (.A({N, S[2:0]}), .Z(Z));

  assign S[3] = N;
endmodule

module incrementador_4 (
  input  [3:0] A,
  output [3:0] S
);

  sumador_4 sumador_4_1 (.Cin(1'b0), .A(4'b0001), .S(S), .B(A));  // open: Cout
  Hex_Digit_Display hex_digit_display_1 (.value(S));  // open: dp
endmodule

module inversor_4 (
  input  [3:0] A,
  input  INV,
  output [3:0] S
);

  wire [3:0] incrementador_4_1_s, not_1_out;

  assign not_1_out = ~A;  // NOT_Gate not_1, 4 bits wide
  incrementador_4 incrementador_4_1 (.A(not_1_out), .S(incrementador_4_1_s));
  Multiplexer #(.width(4)) multiplexer_1 (.in0(A), .in1(incrementador_4_1_s), .out(S), .sel(INV));  // open: en
  Hex_Digit_Display hex_digit_display_1 (.value(S));  // open: dp
endmodule

module ALU (
  input  [3:0] A,
  input  [3:0] B,
  input  [1:0] OP,
  output N,
  output Z,
  output V,
  output C,
  output [3:0] S
);

  wire multiplexer_3_out, overflow_1_ov, RES_cout, SUM_cout;
  wire [3:0] AND_out, inversor_4_1_s, OR_out, RES_s, SUM_s;

  restador_4 RES (.A(A), .B(B), .Cin(1'b0), .Cout(RES_cout), .S(RES_s));
  sumador_4 SUM (.Cin(1'b0), .A(A), .S(SUM_s), .B(B), .Cout(SUM_cout));
  AND_4 AND (.a(A), .b(B), .Out(AND_out));
  OR_4 OR (.a(A), .b(B), .Out(OR_out));
  inversor_4 inversor_4_1 (.A(B), .INV(1'b1), .S(inversor_4_1_s));
  Multiplexer #(.select(2), .width(4), .enable("false")) multiplexer_1 (
    .in0(SUM_s), .in1(RES_s), .in2(AND_out), .in3(OR_out), .out({N, S[2:0]}), .sel(OP));
  Multiplexer #(.select(2), .enable("false")) multiplexer_2 (
    .in0(SUM_cout), .in1(RES_cout), .in2(1'b0), .in3(1'b0), .out(C), .sel(OP));
  overflow overflow_1 (.A_n(A[3]), .B_n(multiplexer_3_out), .S_n(N), .OV(overflow_1_ov));
  Hex_Digit_Display hex_digit_display_1 (.value({N, S[2:0]}));  // open: dp
  Multiplexer #(.select(2), .enable("false")) multiplexer_3 (
    .in0(B[3]), .in1(inversor_4_1_s[3]), .in2(1'b0), .in3(1'b0), .out(multiplexer_3_out), .sel(OP));
  Multiplexer #(.select(2), .enable("false")) multiplexer_4 (
    .in0(overflow_1_ov), .in1(overflow_1_ov), .in2(1'b0), .in3(1'b0), .out(V), .sel(OP));
  comparador_cero comparador_cero_1 (.A({N, S[2:0]}), .Z(Z));

  assign S[3] = N;
endmodule

module verificador (
  output [3:0] a,
  output [3:0] b,
  output [1:0] Op,
  output N,
  output Z,
  output V,
  output C,
  output [3:0] Res,
  output halt
);

  wire clock_1_out;

  Clock clock_1 (.out(clock_1_out));
  Counter #(.width(10), .max('h3ff)) counter_1 (
    .Q({Op, b, a}), .carry(halt), .clk(clock_1_out));  // open: load, D, count, clr
  ALU alu_1 (.A(a), .B(b), .OP(Op), .N(N), .Z(Z), .V(V), .C(C), .S(Res));
endmodule

module overflow (
  input  S_n,
  input  A_n,
  input  B_n,
  output OV
);

  wire and_1_out, and_2_out, not_1_out, not_2_out, not_3_out;

  not not_1 (not_1_out, A_n);
  not not_2 (not_2_out, B_n);
  not not_3 (not_3_out, S_n);
  and and_1 (and_1_out, not_3_out, A_n, B_n);
  and and_2 (and_2_out, S_n, not_1_out, not_2_out);
  or or_1 (OV, and_1_out, and_2_out);
endmodule

module restador_simple (
  input  a,
  input  b,
  output S,
  output Bw
);

  xor xor_1 (S, a, b);
  and and_1 (Bw, ~a, b);  // AND_Gate
endmodule

module restador_completo (
  input  Bwin,
  input  A,
  input  B,
  output R,
  output Bwout
);

  wire restador_simple_1_bw, restador_simple_2_bw, restador_simple_2_s;

  restador_simple restador_simple_1 (.a(restador_simple_2_s), .b(Bwin), .S(R), .Bw(restador_simple_1_bw));
  restador_simple restador_simple_2 (.a(A), .b(B), .S(restador_simple_2_s), .Bw(restador_simple_2_bw));
  or or_1 (Bwout, restador_simple_1_bw, restador_simple_2_bw);
endmodule

module restador_4 (
  input  Cin,
  input  [3:0] A,
  input  [3:0] B,
  output [3:0] S,
  output Cout
);

  wire restador_completo_1_bwout, restador_completo_2_bwout, restador_completo_3_bwout;

  restador_completo restador_completo_1 (.A(A[0]), .B(B[0]), .Bwin(Cin), .R(S[0]), .Bwout(restador_completo_1_bwout));
  restador_completo restador_completo_2 (
    .A(A[1]), .B(B[1]), .Bwin(restador_completo_1_bwout), .R(S[1]), .Bwout(restador_completo_2_bwout));
  restador_completo restador_completo_3 (
    .A(A[2]), .B(B[2]), .Bwin(restador_completo_2_bwout), .R(S[2]), .Bwout(restador_completo_3_bwout));
  restador_completo restador_completo_4 (.A(A[3]), .B(B[3]), .Bwin(restador_completo_3_bwout), .R(S[3]), .Bwout(Cout));
  Hex_Digit_Display hex_digit_display_1 (.value(S));  // open: dp
endmodule

module AND_4 (
  input  [3:0] a,
  input  [3:0] b,
  output [3:0] Out
);

  and and_1 (Out[0], a[0], b[0]);
  and and_2 (Out[1], a[1], b[1]);
  and and_3 (Out[2], a[2], b[2]);
  and and_4 (Out[3], a[3], b[3]);
endmodule

module OR_4 (
  input  [3:0] a,
  input  [3:0] b,
  output [3:0] Out
);

  or or_1 (Out[0], a[0], b[0]);
  or or_2 (Out[1], a[1], b[1]);
  or or_3 (Out[2], a[2], b[2]);
  or or_4 (Out[3], a[3], b[3]);
endmodule
